# Fritzing sketch lcd_thermometer (saved by Fritzing 0.8.7b)
circuit board: 9.08cm x 5.97cm

parts:
  SW1 = Rotary Encoder [part_number=318-ENC130175F-12PS package=encoder]
  ATMega328p = atmega328p [package=dip]
  R10 = Resistor [tolerance=±5% resistance=4.7k package=THT]
  R9 = Resistor [tolerance=±5% resistance=4.7k package=THT]
  D1 = Schottky Diode [part_number=1N5817 package="300 mil [THT]"]
  R14 = Resistor [tolerance=±0.1% resistance=8.2k package="0603 [SMD]"]
  R17 = Resistor [tolerance=±0.1% resistance=8.2k package="0603 [SMD]"]
  R20 = Resistor [tolerance=±5% resistance=10k package=THT]
  Q2 = MOSFET-NCHANNEL [package=sot23-3]
  R23 = Resistor [tolerance=±5% resistance=10k package=THT]
  C18 = Ceramic Capacitor [capacitance=10nF voltage=10V package="100 mil [THT, multilayer]"]
  R24 = Resistor [tolerance=±5% resistance=1k package=THT]
  C17 = Electrolytic Capacitor [capacitance=1µF package="100 mil [THT, electrolytic]"]
  D10 = Diode [part_number=Schottky package=sod-323]
  JP1 = female pin header, 8 pins [form="♀ (female)"]
  GND = male pin header, 1 pin [form="♂ (male)"]
  Vcc = male pin header, 1 pin [form="♂ (male)"]
  Contrast_Adj = Square Sealed Panel Control [part_number=3310P-001-103L package="TO92 [THT]"]
  R18 = Resistor [tolerance=±0.1% resistance=100k package="0603 [SMD]"]
  OneWire_#2 = screw terminal, 3 pins
  OneWire_#1 = screw terminal, 3 pins
  R19 = Resistor [tolerance=±5% resistance=1k package=THT]
  C20 = Ceramic Capacitor [capacitance=10nF voltage=10V package="100 mil [THT, multilayer]"]
  Q4 = MOSFET-NCHANNEL [package=sot23-3]
  XTAL1 = Crystal [frequency="16 Mhz" package=THT]
  C4 = Ceramic Capacitor [capacitance=10pF package="100 mil [THT, multilayer]"]
  C3 = Ceramic Capacitor [capacitance=10pF package="100 mil [THT, multilayer]"]
  C9 = Ceramic Capacitor [capacitance=10µF voltage=10V package="200 mil [THT, multilayer]"]
  D21 = Schottky Diode [part_number=1N5817 package="300 mil [THT]"]
  C19 = Ceramic Capacitor [capacitance=10nF voltage=10V package="100 mil [THT, multilayer]"]
  LED1 = LED - 5mm [color="Red (633nm)" package="5 mm [THT]"]
  R38 = Resistor [tolerance=±5% resistance=220 package=THT]
  GND_2 = male pin header, 1 pin [form="♂ (male)"]
  GND_3 = male pin header, 1 pin [form="♂ (male)"]
  GND_4 = male pin header, 1 pin [form="♂ (male)"]
  GND_5 = male pin header, 1 pin [form="♂ (male)"]
  GND_6 = male pin header, 1 pin [form="♂ (male)"]
  GND_7 = male pin header, 1 pin [form="♂ (male)"]
  GND_8 = male pin header, 1 pin [form="♂ (male)"]
  GND_9 = male pin header, 1 pin [form="♂ (male)"]
  GND_10 = male pin header, 1 pin [form="♂ (male)"]
  GND_11 = male pin header, 1 pin [form="♂ (male)"]
  GND_12 = male pin header, 1 pin [form="♂ (male)"]
  GND_13 = male pin header, 1 pin [form="♂ (male)"]
  D11 = Diode [package=sod-323]
  C21 = Ceramic Capacitor [capacitance=3.3pF voltage=100V package="0603 [SMD, multilayer]"]
  C22 = Ceramic Capacitor [capacitance=3.3pF voltage=100V package="0603 [SMD, multilayer]"]
  R16 = Resistor [tolerance=±0.1% resistance=15k package="0603 [SMD]"]
  C23 = Ceramic Capacitor [capacitance=3.3pF voltage=100V package="0603 [SMD, multilayer]"]
  C24 = Ceramic Capacitor [capacitance=3.3pF voltage=100V package="0603 [SMD, multilayer]"]
  R13 = Resistor [tolerance=±0.1% resistance=560 package="0603 [SMD]"]
  GND_14 = male pin header, 1 pin [form="♂ (male)"]
  GND_15 = male pin header, 1 pin [form="♂ (male)"]
  LCD3 = LCD screen
  TL431 = Programmable Precision Reference [part_number=TL431 package="TO92 [THT]"]
  GND_16 = male pin header, 1 pin [form="♂ (male)"]
  D22 = Diode [part_number=Schottky package=sod-323]
  D23 = Diode [part_number=Schottky package=sod-323]
  GND_17 = male pin header, 1 pin [form="♂ (male)"]
  R39 = Resistor [tolerance=±5% resistance=10k package=THT]
  TP5 = Test Point
  TP9 = Test Point
  TP8 = Test Point
  TP4 = Test Point
  TP14 = Test Point
  TP22 = Test Point
  TP25 = Test Point
  TP20 = Test Point
  TP10 = Test Point
  TP19 = Test Point
  TP18 = Test Point
  TP17 = Test Point
  TP16 = Test Point
  TP15 = Test Point
  TP24 = Test Point
  TP21 = Test Point
  TP23 = Test Point
  TP1 = Test Point
  Q5 = MOSFET-NCHANNEL [package=sot23-3]
  R41 = Resistor [tolerance=±5% resistance=1k package=THT]
  R40 = Resistor [tolerance=±5% resistance=10k package=THT]
  GND_18 = male pin header, 1 pin [form="♂ (male)"]
  GND_19 = male pin header, 1 pin [form="♂ (male)"]
  TP3 = Test Point
  GND_20 = male pin header, 1 pin [form="♂ (male)"]
  Pad5 = Pad [width=1.18749168386798 height=1.09250017108322 connect=center]
  Pad6 = Pad [width=1.18749168386798 height=1.09250017108322 connect=center]
  Pad7 = Pad [width=1.18749168386798 height=1.09250017108322 connect=center]
  Pad8 = Pad [width=1.18749168386798 height=1.09250017108322 connect=center]
  Pad9 = Pad [width=1.18749168386798 height=1.09250017108322 connect=center]
  Pad10 = Pad [width=1.18749168386798 height=1.09250017108322 connect=center]
  Pad11 = Pad [width=1.18749168386798 height=1.09250017108322 connect=center]
  Pad12 = Pad [width=1.18749168386798 height=1.09250017108322 connect=center]
  Pad13 = Pad [width=1.18749168386798 height=1.09250017108322 connect=center]
  Pad14 = Pad [width=1.18749168386798 height=1.09250017108322 connect=center]
  Pad15 = Pad [width=1.18749168386798 height=1.09250017108322 connect=center]
  Pad16 = Pad [width=1.18749168386798 height=1.09250017108322 connect=center]
  Pad17 = Pad [width=1.18749168386798 height=1.09250017108322 connect=center]
  Pad18 = Pad [width=1.18749168386798 height=1.09250017108322 connect=center]
  Pad19 = Pad [width=1.18749168386798 height=1.09250017108322 connect=center]
  Pad20 = Pad [width=1.18749168386798 height=1.09250017108322 connect=center]
  Pad22 = Pad [width=1.18749168386798 height=1.09250017108322 connect=center]
  Pad21 = Pad [width=1.18749168386798 height=1.09250017108322 connect=center]
  Pad23 = Pad [width=1.18749168386798 height=1.09250017108322 connect=center]
  Pad24 = Pad [width=1.18749168386798 height=1.09250017108322 connect=center]
  Pad26 = Pad [width=1.18749168386798 height=1.09250017108322 connect=center]
  Pad25 = Pad [width=1.18749168386798 height=1.09250017108322 connect=center]
  Pad27 = Pad [width=1.18749168386798 height=1.09250017108322 connect=center]
  Pad28 = Pad [width=1.18749168386798 height=1.09250017108322 connect=center]
  Pad29 = Pad [width=1.18749168386798 height=1.09250017108322 connect=center]
  Pad30 = Pad [width=1.18749168386798 height=1.09250017108322 connect=center]
  Pad32 = Pad [width=1.3 height=1.3 connect=center]
  Pad33 = Pad [width=1.3 height=1.3 connect=center]
  Pad34 = Pad [width=1.3 height=2 connect=center]

nets:
  N1: SW1.X, ATMega328p.D4, TP10.test_pad
  GND: SW1.Y, SW1.C, SW1.GND, ATMega328p.GND, R20.Pin_0, Q2.S, R23.Pin_0, C18.1, C17.-, JP1.pin6, GND.pin1, C20.1, Q4.S, C4.1, C3.1, D21.anode, C19.1, LED1.cathode, GND_2.pin1, GND_3.pin1, GND_4.pin1, GND_5.pin1, GND_6.pin1, GND_7.pin1, GND_8.pin1, GND_9.pin1, GND_10.pin1, GND_11.pin1, GND_12.pin1, GND_13.pin1, C21.1, C22.1, C23.1, C24.1, GND_14.pin1, GND_15.pin1, LCD3.GND#16, LCD3.GND#17, LCD3.GND#18, LCD3.GND#19, GND_16.pin1, GND_17.pin1, Q5.S, R40.Pin_0, GND_18.pin1, GND_19.pin1, GND_20.pin1, Pad7.pad, Pad10.pad, Pad18.pad, Pad25.pad
  N2: SW1.A, ATMega328p.D3_(PWM), TP8.test_pad
  N3: SW1.B, ATMega328p.D2, TP9.test_pad
  N4: ATMega328p.RESET, C9.0, R39.Pin_0, Pad5.pad, Pad14.pad
  N5: ATMega328p.D0_(RX), JP1.pin3, C21.0
  N6: ATMega328p.D1_(TX), JP1.pin2, C22.0
  5V: ATMega328p.VCC, ATMega328p.AVCC, R10.Pin_1, R9.Pin_1, D1.cathode, JP1.pin4, Contrast_Adj.CW, OneWire_#2.pin3, OneWire_#1.pin3, C20.0, D21.cathode, C19.0, R13.Pin_0, LCD3.VDD, D22.C, D23.C, R39.Pin_1, TP1.test_pad, Pad8.pad, Pad13.pad, Pad19.pad, Pad28.pad, Pad30.pad, Pad33.pad
  N7: ATMega328p.XLAT1, XTAL1.pin_1, C4.0
  N8: ATMega328p.XLAT2, XTAL1.pin_0, C3.0
  N9: ATMega328p.D5_(PWM), LCD3.DB4, TP15.test_pad
  N10: ATMega328p.D6_(PWM), LCD3.DB5, TP16.test_pad
  N11: ATMega328p.D7, LCD3.DB6, TP17.test_pad
  N12: ATMega328p.D8, LCD3.DB7, TP18.test_pad
  N13: ATMega328p.D9_(PWM), LCD3.LED+, TP19.test_pad
  N14: ATMega328p.D10_(PWM), R9.Pin_0, D10.C, OneWire_#2.pin2, D22.A, Pad20.pad
  N15: ATMega328p.D11_(PWM), R10.Pin_0, OneWire_#1.pin2, D11.C, D23.A, Pad29.pad
  N16: ATMega328p.D12, R19.Pin_0, TP3.test_pad, Pad12.pad
  N17: ATMega328p.D13, R38.Pin_0, TP20.test_pad, R41.Pin_0, Pad21.pad, Pad24.pad
  N18: ATMega328p.AREF, R14.Pin_0, C18.0, R13.Pin_1, TL431.K, TP25.test_pad
  N19: ATMega328p.A0, R17.Pin_0, R18.Pin_0
  N20: ATMega328p.A1, LCD3.RS, TP23.test_pad
  N21: ATMega328p.A2, LCD3.E, TP24.test_pad
  N22: ATMega328p.A3, R24.Pin_0, TP4.test_pad, Pad15.pad
  N23: ATMega328p.A4_(SDA), JP1.pin8, C23.0
  N24: ATMega328p.A5_(SCL), JP1.pin7, C24.0
  N25: D1.anode, R17.Pin_1, C17.+, Vcc.pin1, TP14.test_pad, Pad27.pad
  N26: R14.Pin_1, R16.Pin_0, TL431.R, TP5.test_pad
  N27: R20.Pin_1, Q2.G, R19.Pin_1, Pad9.pad, Pad11.pad
  LCDLowSideSwitch: Q2.D, Contrast_Adj.CCW, LCD3.GND#0, LCD3.R/W, LCD3.LED-, TP21.test_pad, Pad32.pad
  N28: R23.Pin_1, R24.Pin_1, Q4.G, Pad16.pad, Pad17.pad
  OWBLowSideSwitch: D10.A, OneWire_#2.pin1, OneWire_#1.pin1, D11.A, Q5.D
  N29: JP1.pin1, C9.1, Pad6.pad
  N30: Contrast_Adj.Wiper, LCD3.V0, Pad34.pad
  ArefLowSideSwitch: R18.Pin_1, Q4.D, R16.Pin_1, TL431.A, TP22.test_pad
  N31: LED1.anode, R38.Pin_1, Pad22.pad
  N32: Q5.G, R41.Pin_1, R40.Pin_1, Pad23.pad, Pad26.pad

notes:
  +
  -
  Copyright
  2014
  Chris
  Evich
  lcd_thermometer, Copyright 2014 Chris Evich, 2.5
  Battery Voltage Sense
  Battery connector
  Prog./Debug. Connector
  3.8589 volt reference
  OW Bus A
  OW Bus B
  Rotary Encoder w/ Botton
  Contrast Adjust
  DTR
  RX
  TX
  +5v
  N/C
  GND
  SCL
  SDA
  G
  D
  Thir Mom'tr
  rev. 2.5
  +5v Supply
  Close to Vcc
  Close to AVcc
  2.495 * (1 + (R14 / R16))
  (R18 / (R17 + R18)) * Vcc
  6.5v => 3.5714
  4.0v => 2.1978
  R41
  R38
  R39
  D1
  +5v Reg
  IN
  OUT

custom parts:
  Rotary Encoder: This is a 12-step rotary encoder with a nice ‘clicking’ feel. It’s breadboard friendly, and has a pretty handy select switch (by pushing in on the knob). The encoder is different from a potentiometer in that an encoder has full rotation without limits. The unit outputs gray code so that you can tell how much and in which direction the encoder has been turned.
  atmega328p: Atmel ATmega328 microcontroller. The hardware hacker favorite.
  Square Sealed Panel Control: * Conductive plastic * PC board and bushing mount * Plastic or metal bushing and plastic shaft * Withstands typical industrial washing processes * Compact package saves board and panel space
  LCD screen: A standard character display, usually with 2x16 characters. Comes in many colors.
  Programmable Precision Reference: Three-terminal programmable precision voltage reference.
